# Fritzing sketch Sketch (saved by Fritzing 0.9.3b)
breadboards: 1

parts:
  Q2 = Basic FET N-Channel [package="D2Pak [SMD]"]
  U1 = attiny85 [package=dip]
  220_Ohm_Resistor = Resistor [tolerance=±5% resistance=220 package=THT]
  220_Ohm_Resistor1 = Resistor [tolerance=±5% resistance=100 package=THT]
  VCC1 = 4 x AAA Battery Mount
  Bauteil1 = Arduino Uno (Rev3)
  Bauteil3 = Arduino Cellular Shield
  Bauteil4 = dfHX711 Weighing Sensor Module

nets:
  N1: Q2.Gate, 220_Ohm_Resistor.Pin_1
  GND: Q2.drain, Bauteil1.GND, Bauteil3.GND, Bauteil4.GND
  N2: Q2.source, U1.Pin_4, 220_Ohm_Resistor1.Pin_0, VCC1.-
  N3: U1.Pin_5, 220_Ohm_Resistor.Pin_0, 220_Ohm_Resistor1.Pin_1
  5V: U1.Pin_8, VCC1.+, Bauteil1.5V, Bauteil3.5V, Bauteil4.VCC
  N4: Bauteil1.D9_PWM, Bauteil3.A2
  N5: Bauteil1.D5_PWM, Bauteil4.SCK
  N6: Bauteil1.D6_PWM, Bauteil4.DOUT

notes:
  LOAD CELL

custom parts:
  dfHX711 Weighing Sensor Module: HX711 is a precision 24-bit analog-to-digital converter (ADC) designed for weigh scales and industrial control applications to interface directly with a bridge sensor.
